# Fritzing sketch UNO2UNO_I2C+IO (saved by Fritzing 0.9.3b)

parts:
  Master = Arduino Uno (Rev3)
  Slave = Arduino Uno (Rev3)

nets:
  N1: Master.A0, Slave.A0
  N2: Master.A4/SDA, Slave.A4/SDA
  N3: Master.A5/SCL, Slave.A5/SCL
  N4: Master.D12/MISO, Slave.D12/MISO
  GND: Master.GND, Slave.GND
  N5: Master.D2, Slave.D2
  5V: Master.5V, Slave.VIN

notes:
  Slave
  Controller
  USB
  Fertigung
  power
  COMx
  . . .
  12 Verbindungen
  I2C
  Power
