# Fritzing sketch UNO2UNO_I2C (saved by Fritzing 0.9.3b)

parts:
  Master = Arduino Uno (Rev3)
  Slave = Arduino Uno (Rev3)

nets:
  N1: Master.A4/SDA, Slave.A4/SDA
  N2: Master.A5/SCL, Slave.A5/SCL
  GND: Master.GND, Slave.GND
  5V: Master.5V, Slave.VIN

notes:
  Slave
  Controller (I2C master)
  USB
  House (I2C slave)
  power
  COMx
