# Fritzing sketch Read_MPU_6050 (saved by Fritzing 0.9.4)
breadboards: 1

parts:
  Bauteil2 = Tri-Axis Gyro Breakout - L3G4200D
  C1 = Electrolytic Capacitor [capacitance=100µF voltage=10V package="100 mil [THT, electrolytic]"]
  Bauteil3 = Arduino Nano (Rev3.0)

nets:
  GND: Bauteil2.GND, C1.-, Bauteil3.GND
  VCC: Bauteil2.VCC, Bauteil3.3V3
  N1: Bauteil2.SCL, Bauteil3.A5
  N2: Bauteil2.SDA, Bauteil3.A4
  N3: C1.+, Bauteil3.5V

notes:
  MPU 6050
