# Fritzing sketch UNO2UNO_I2C+IO (saved by Fritzing 0.9.4)

parts:
  Master = Arduino Uno (Rev3)
  Slave = Arduino Uno (Rev3)

nets:
  N1: Master.A4/SDA, Slave.A4/SDA
  N2: Master.A5/SCL, Slave.A5/SCL
  N3: Master.D8, Slave.D8
  GND: Master.GND, Slave.GND
  N4: Master.D2, Slave.D2
  5V: Master.5V, Slave.VIN

notes:
  Slave
  Controller
  USB
  Washing Maschine
  power
  COMx
  . . .
  7 Verbindungen
  I2C
  Power
  Plant
